// Logisim project fpu.circ as structural Verilog: 14 circuits, main circuit main
module main (
  input  in_1,
  input  [15:0] in_2,
  input  [15:0] in_3,
  output [15:0] out_4
);

  // fpu fpu_1: pin names not known; wires that end beside it: in_2[0], in_2[5:1], in_2[15:6], in_3[0], in_3[5:1], in_3[15:6], in_1, out_4[15], out_4[14:10], out_4[9:0]
endmodule

module fpu (
  input  Operation,
  input  Znak_A,
  input  [4:0] \Wykładnik_A ,
  input  [9:0] Mantysa_A,
  input  Znak_B,
  input  [4:0] \Wykładnik_B ,
  input  [9:0] Mantysa_B,
  output Znak,
  output [15:0] out_9,
  output [4:0] out_10
);

  wire expoffset_1_out_3;
  wire [1:0] operationselector_1_operation;
  wire [3:0] expoffset_1_out_4, normalizator_1_count;
  wire [4:0] expoffset_1_out_5;
  wire [15:0] extendwithone_1_output, extendwithone_2_output, mantissaselector_1_offseted_a,
       mantissaselector_1_offseted_b, operation_1_a_op_b;

  OperationSelector operationselector_1 (
    .Operacja(Operation), .Znak_A(Znak_A), .Znak_B(Znak_B), .Operation(operationselector_1_operation));
  ExtendWithOne extendwithone_1 (.Input(Mantysa_A), .Output(extendwithone_1_output), .\Wykładnik (\Wykładnik_A ));
  ExtendWithOne extendwithone_2 (.Input(Mantysa_B), .Output(extendwithone_2_output), .\Wykładnik (\Wykładnik_B ));
  ExpOffset expoffset_1 (
    .in_1(\Wykładnik_A ), .in_2(\Wykładnik_B ), .out_3(expoffset_1_out_3), .out_4(expoffset_1_out_4),
    .out_5(expoffset_1_out_5));
  MantissaSelector mantissaselector_1 (
    .A(extendwithone_1_output), .B(extendwithone_2_output), .which(expoffset_1_out_3),
    .Shift(expoffset_1_out_4), .Offseted_A(mantissaselector_1_offseted_a),
    .Offseted_B(mantissaselector_1_offseted_b));
  Operation operation_1 (
    .Operation(operationselector_1_operation), .A(mantissaselector_1_offseted_a),
    .B(mantissaselector_1_offseted_b), .A_op_B(operation_1_a_op_b), .Znak(Znak));  // open: overflow
  normalizator normalizator_1 (
    .in_1(operation_1_a_op_b), .in_2({16{1'b0}}), .shifted(out_9), .count(normalizator_1_count));
  ExponentialCalc exponentialcalc_1 (
    .Offset_Count(normalizator_1_count), .out_5(out_10), .in_2(expoffset_1_out_5), .in_3(\Wykładnik_B ),
    .in_4(\Wykładnik_A ));
  // NOT_Gate not_1 is placed but not wired
endmodule

module abs (
  input  [4:0] in_1,
  output [3:0] out_2
);

  wire [4:0] negator_1_out;
  wire [4:4] multiplexer_1_out;

  Negator #(.width(5)) negator_1 (.in(in_1), .out(negator_1_out));
  Multiplexer #(.width(5), .disabled(0), .enable("false")) multiplexer_1 (
    .in0(in_1), .in1(negator_1_out), .out({multiplexer_1_out[4], out_2}), .sel(in_1[4]));

  // Notes on the sheet:
  //   Przyjmuje 5cio bitową liczbę i zwraca 4-bitową wartość bezwzględną
  //   Jeżeli ostatni bit==1 -> odejmij jeden, odwróć. w przeciwnym razie zwróć liczbę i obetnij ostatni bit.
endmodule

module ExtendWithOne (
  input  [9:0] Input,
  input  [4:0] \Wykładnik ,
  output [15:0] Output
);

  wire or_1_out;
  wire [10:0] bit_extender_1_out, bit_extender_2_out, multiplexer_1_out;

  or or_1 (or_1_out, \Wykładnik [0], \Wykładnik [1], \Wykładnik [2], \Wykładnik [3], \Wykładnik [4]);
  assign bit_extender_1_out = {{1{1'b0}}, Input};  // Bit_Extender bit_extender_1
  Multiplexer #(.width(11), .enable("false")) multiplexer_1 (
    .in0(bit_extender_1_out), .in1(bit_extender_2_out), .out(multiplexer_1_out), .sel(or_1_out));
  assign bit_extender_2_out = {{1{1'b1}}, Input};  // Bit_Extender bit_extender_2
  assign Output = {{5{1'b0}}, multiplexer_1_out};  // Bit_Extender bit_extender_3

  // Notes on the sheet:
  //   Tylko Manipulacja bitami. Dodaje z lewej strony liczby 6 nowych bitów o wartościach: 000 001
endmodule

module normalizator (
  input  [15:0] in_1,
  input  [15:0] in_2,
  output [15:0] shifted,
  output [3:0] count
);

  wire normalizerunit_1_end, normalizerunit_2_end, normalizerunit_3_end, normalizerunit_4_end,
       normalizerunit_5_end, normalizerunit_6_end, normalizerunit_7_end, normalizerunit_8_end,
       normalizerunit_9_end, normalizerunit_10_end, normalizerunit_11_end, normalizerunit_12_end,
       normalizerunit_13_end, normalizerunit_14_end, priority_encoder_1_p1, priority_encoder_1_p17,
       priority_encoder_1_p18;
  wire [3:0] priority_encoder_1_p10;
  wire [15:0] normalizerunit_1_out, normalizerunit_1_outputbus_2, normalizerunit_2_out,
       normalizerunit_2_outputbus_2, normalizerunit_3_out, normalizerunit_3_outputbus_2,
       normalizerunit_4_out, normalizerunit_4_outputbus_2, normalizerunit_5_out,
       normalizerunit_5_outputbus_2, normalizerunit_6_out, normalizerunit_6_outputbus_2,
       normalizerunit_7_out, normalizerunit_7_outputbus_2, normalizerunit_8_out,
       normalizerunit_8_outputbus_2, normalizerunit_9_out, normalizerunit_9_outputbus_2,
       normalizerunit_10_out, normalizerunit_10_outputbus_2, normalizerunit_11_out,
       normalizerunit_11_outputbus_2, normalizerunit_12_out, normalizerunit_12_outputbus_2,
       normalizerunit_13_out, normalizerunit_13_outputbus_2, normalizerunit_14_out,
       normalizerunit_14_outputbus_2, normalizerunit_16_out, normalizerunit_16_outputbus_2;

  normalizerUnit normalizerunit_1 (
    .In(normalizerunit_2_out), .OutputBus(normalizerunit_2_outputbus_2), .Out(normalizerunit_1_out),
    .End(normalizerunit_1_end), .OutputBus_2(normalizerunit_1_outputbus_2));
  normalizerUnit normalizerunit_2 (
    .In(in_1), .OutputBus(in_2), .Out(normalizerunit_2_out), .End(normalizerunit_2_end),
    .OutputBus_2(normalizerunit_2_outputbus_2));
  normalizerUnit normalizerunit_3 (
    .In(normalizerunit_4_out), .OutputBus(normalizerunit_4_outputbus_2), .Out(normalizerunit_3_out),
    .End(normalizerunit_3_end), .OutputBus_2(normalizerunit_3_outputbus_2));
  normalizerUnit normalizerunit_4 (
    .In(normalizerunit_1_out), .OutputBus(normalizerunit_1_outputbus_2), .Out(normalizerunit_4_out),
    .End(normalizerunit_4_end), .OutputBus_2(normalizerunit_4_outputbus_2));
  normalizerUnit normalizerunit_5 (
    .In(normalizerunit_3_out), .OutputBus(normalizerunit_3_outputbus_2), .Out(normalizerunit_5_out),
    .End(normalizerunit_5_end), .OutputBus_2(normalizerunit_5_outputbus_2));
  normalizerUnit normalizerunit_6 (
    .In(normalizerunit_5_out), .OutputBus(normalizerunit_5_outputbus_2), .Out(normalizerunit_6_out),
    .End(normalizerunit_6_end), .OutputBus_2(normalizerunit_6_outputbus_2));
  normalizerUnit normalizerunit_7 (
    .In(normalizerunit_6_out), .OutputBus(normalizerunit_6_outputbus_2), .Out(normalizerunit_7_out),
    .End(normalizerunit_7_end), .OutputBus_2(normalizerunit_7_outputbus_2));
  normalizerUnit normalizerunit_8 (
    .In(normalizerunit_7_out), .OutputBus(normalizerunit_7_outputbus_2), .Out(normalizerunit_8_out),
    .End(normalizerunit_8_end), .OutputBus_2(normalizerunit_8_outputbus_2));
  normalizerUnit normalizerunit_9 (
    .In(normalizerunit_10_out), .OutputBus(normalizerunit_10_outputbus_2), .Out(normalizerunit_9_out),
    .End(normalizerunit_9_end), .OutputBus_2(normalizerunit_9_outputbus_2));
  normalizerUnit normalizerunit_10 (
    .In(normalizerunit_8_out), .OutputBus(normalizerunit_8_outputbus_2), .Out(normalizerunit_10_out),
    .End(normalizerunit_10_end), .OutputBus_2(normalizerunit_10_outputbus_2));
  normalizerUnit normalizerunit_11 (
    .In(normalizerunit_12_out), .OutputBus(normalizerunit_12_outputbus_2), .Out(normalizerunit_11_out),
    .End(normalizerunit_11_end), .OutputBus_2(normalizerunit_11_outputbus_2));
  normalizerUnit normalizerunit_12 (
    .In(normalizerunit_9_out), .OutputBus(normalizerunit_9_outputbus_2), .Out(normalizerunit_12_out),
    .End(normalizerunit_12_end), .OutputBus_2(normalizerunit_12_outputbus_2));
  normalizerUnit normalizerunit_13 (
    .In(normalizerunit_11_out), .OutputBus(normalizerunit_11_outputbus_2), .Out(normalizerunit_13_out),
    .End(normalizerunit_13_end), .OutputBus_2(normalizerunit_13_outputbus_2));
  normalizerUnit normalizerunit_14 (
    .In(normalizerunit_13_out), .OutputBus(normalizerunit_13_outputbus_2), .Out(normalizerunit_14_out),
    .End(normalizerunit_14_end), .OutputBus_2(normalizerunit_14_outputbus_2));
  // Priority_Encoder #(.select(4)) priority_encoder_1: pin names not known; wires that end beside it: priority_encoder_1_p1, normalizerunit_2_end, normalizerunit_1_end, normalizerunit_4_end, normalizerunit_3_end, normalizerunit_5_end, normalizerunit_6_end, normalizerunit_7_end, normalizerunit_8_end, priority_encoder_1_p10, normalizerunit_10_end, normalizerunit_9_end, normalizerunit_12_end, normalizerunit_11_end, normalizerunit_13_end, normalizerunit_14_end, priority_encoder_1_p17, priority_encoder_1_p18
  normalizerUnit normalizerunit_15 (
    .In(normalizerunit_16_out), .OutputBus(normalizerunit_16_outputbus_2), .End(priority_encoder_1_p18),
    .OutputBus_2(shifted));  // open: Out
  normalizerUnit normalizerunit_16 (
    .In(normalizerunit_14_out), .OutputBus(normalizerunit_14_outputbus_2), .Out(normalizerunit_16_out),
    .End(priority_encoder_1_p17), .OutputBus_2(normalizerunit_16_outputbus_2));
  Multiplexer #(.width(4), .enable("false")) multiplexer_1 (
    .in0(priority_encoder_1_p10), .in1(4'b0101), .out(count), .sel(priority_encoder_1_p1));
endmodule

module ExpOffset (
  input  [4:0] in_1,
  input  [4:0] in_2,
  output out_3,
  output [3:0] out_4,
  output [4:0] out_5
);

  Subtractor #(.width(5)) subtractor_1 (.a(in_1), .b(in_2), .out({out_3, out_5[3:0]}));  // open: bin, bout
  abs abs_1 (.in_1({out_3, out_5[3:0]}), .out_2(out_4));

  assign out_5[4] = out_3;

  // Notes on the sheet:
  //   To są zwykłe addery ustawione na odejmowanie na stałe.
  //   Różnica w U2
  //   To jest bit znaku (czwarty z outputu liczcą od zera)
endmodule

module MantissaSelector (
  input  [15:0] A,
  input  [15:0] B,
  input  which,
  input  [3:0] Shift,
  output [15:0] Offseted_A,
  output [15:0] Offseted_B
);

  wire [3:0] multiplexer_1_out, multiplexer_2_out;

  Multiplexer #(.width(4), .enable("false")) multiplexer_1 (
    .in0(Shift), .in1(4'b0000), .out(multiplexer_1_out), .sel(which));
  Multiplexer #(.width(4), .enable("false")) multiplexer_2 (
    .in0(4'b0000), .in1(Shift), .out(multiplexer_2_out), .sel(which));
  Shifter_part #(.width(16)) shifter_1 (.in(A), .\dist (multiplexer_1_out), .out(Offseted_A));
  Shifter_part #(.width(16), .shift("lr")) shifter_2 (.in(B), .\dist (multiplexer_2_out), .out(Offseted_B));

  // Notes on the sheet:
  //   Ta maszynka przyjmuje dwie 16-bitowe liczby i przesuwa jedną znich w prawo o wartość Shift
  //   Która liczba zostanie przesunięta, definiuje wejście which, jak 0 przesunie A, jak 1 przesunie B
endmodule

module ExponentialCalc (
  input  [3:0] Offset_Count,
  input  [4:0] in_2,
  input  [4:0] in_3,
  input  [4:0] in_4,
  output [4:0] out_5
);

  wire comparator_1_gt, or_1_out, or_2_out, or_3_out;
  wire [4:0] bit_extender_1_out, multiplexer_1_out, multiplexer_2_out, subtractor_1_out;

  assign bit_extender_1_out = {{1{1'b0}}, Offset_Count};  // Bit_Extender bit_extender_1
  Subtractor #(.width(5)) subtractor_1 (
    .a(5'b00101), .b(bit_extender_1_out), .out(subtractor_1_out));  // open: bin, bout
  or or_1 (or_1_out, in_3[0], in_3[1], in_3[2], in_3[3], in_3[4]);
  or or_2 (or_2_out, in_4[0], in_4[1], in_4[2], in_4[3], in_4[4]);
  or or_3 (or_3_out, or_1_out, or_2_out);
  Multiplexer #(.width(5), .enable("false")) multiplexer_1 (
    .in0({5{1'b0}}), .in1(subtractor_1_out), .out(multiplexer_1_out), .sel(or_3_out));
  Comparator #(.width(5), .mode("unsigned")) comparator_1 (.a(in_3), .b(in_4), .gt(comparator_1_gt));  // open: eq, lt
  Multiplexer #(.width(5), .enable("false")) multiplexer_2 (
    .in0(in_3), .in1(in_4), .out(multiplexer_2_out), .sel(comparator_1_gt));
  Adder #(.width(5)) adder_1 (.a(multiplexer_1_out), .b(multiplexer_2_out), .out(out_5));  // open: cin, cout

  // Notes on the sheet:
  //   Note: Przy obu zdenormalizowanych odejmować 6 a nie 5
endmodule

module Operation (
  input  [1:0] Operation,
  input  [15:0] A,
  input  [15:0] B,
  output [15:0] A_op_B,
  output overflow,
  output Znak
);

  Adder #(.width(16)) adder_1 (.a(A), .b(B), .out(A_op_B), .cout(overflow));  // open: cin

  assign Znak = 1'b0;
endmodule

module OperationSelector (
  input  Operacja,
  input  Znak_A,
  input  Znak_B,
  output [1:0] Operation
);
endmodule

module Shifter (
  input  Cin,
  input  [15:0] in_2,
  output [15:0] out,
  output Cout
);


  assign Cout = in_2[15];
  assign out = {in_2[14:0], Cin};
endmodule

module normalizerUnit (
  input  [15:0] In,
  input  [15:0] OutputBus,
  output [15:0] Out,
  output End,
  output [15:0] OutputBus_2
);

  wire not_1_out;
  wire [15:0] multiplexer_1_out, shifter_1_out;

  Shifter shifter_1 (.Cin(1'b0), .in_2(In), .out(shifter_1_out), .Cout(End));
  not not_1 (not_1_out, End);
  Multiplexer #(.width(16), .enable("false")) multiplexer_1 (
    .in0({16{1'b0}}), .in1(shifter_1_out), .out(multiplexer_1_out), .sel(End));
  Multiplexer #(.width(16), .enable("false")) multiplexer_2 (
    .in0({16{1'b0}}), .in1(shifter_1_out), .out(Out), .sel(not_1_out));
  assign OutputBus_2 = multiplexer_1_out | OutputBus;  // OR_Gate or_1, 16 bits wide
endmodule

module halfadders (
  input  in_1,
  input  in_2,
  output out_3,
  output out_4
);

  xor xor_1 (out_3, in_1, in_2);
  and and_1 (out_4, in_2, in_1);
endmodule

module rhalfadder (
  input  in_1,
  input  in_2,
  input  in_3,
  input  in_4,
  output out_5,
  output out_6,
  output out_7
);

  wire halfadders_1_out_4, halfadders_2_out_4;

  halfadders halfadders_1 (.in_1(in_2), .in_2(in_1), .out_3(out_5), .out_4(halfadders_1_out_4));
  halfadders halfadders_2 (.in_1(in_3), .in_2(halfadders_1_out_4), .out_3(out_6), .out_4(halfadders_2_out_4));
  halfadders halfadders_3 (.in_1(in_4), .in_2(halfadders_2_out_4), .out_3(out_7));  // open: out_4
endmodule
