// Logisim project fpu2 — kopia.circ as structural Verilog: 10 circuits, main circuit main
module main (
  input  [1:0] op,
  input  [15:0] InA,
  input  [15:0] InB,
  output [15:0] Out
);

  fpu fpu_1 (
    .out_8(Out[15]), .out_9(Out[9:0]), .out_10(Out[14:10]), .in_1(op), .Znak_A(InA[15]),
    .Wykladnik_A(InA[14:10]), .Mantysa_A(InA[9:0]), .Znak_B(InB[15]), .Wykladnik_B(InB[14:10]),
    .Mantysa_B(InB[9:0]));
  // Probe on Out
endmodule

module fpu (
  input  [1:0] in_1,
  input  Znak_A,
  input  [4:0] Wykladnik_A,
  input  [9:0] Mantysa_A,
  input  Znak_B,
  input  [4:0] Wykladnik_B,
  input  [9:0] Mantysa_B,
  output out_8,
  output [9:0] out_9,
  output [4:0] out_10
);

  wire and_1_out, and_2_out, comparator_1_lt, comparator_2_gt, decoder_1_out0, decoder_1_out1,
       exponentcalc_1_out_3, exponentcalc_1_out_6, exponentcalc_1_out_7, expsign_1_add_sub, expsign_1_sign,
       normalizer_1_out_4, not_1_out, not_2_out, not_3_out, op_1_carry, or_1_out, or_2_out, or_3_out,
       xor_1_out;
  wire [3:0] exponentcalc_1_out_4, normalizer_1_out_3, normalizer_2_out_3, subtractor_3_out;
  wire [4:0] adder_1_out, adder_2_out, adder_3_out, bit_extender_1_out, bit_extender_2_out,
       multiplexer_1_out, multiplexer_3_out, multiplexer_5_out, subtractor_1_out;
  wire [5:0] multiplexer_4_out, subtractor_2_out;
  wire [5:5] adder_2_cout;
  wire [7:0] multiplier_1_cout, multiplier_1_out;
  wire [15:0] ExtA, ExtB, normalizer_1_out_2, normalizer_2_out_2, op_1_out_4, shifter_1_out_5,
       shifter_1_out_6;
  wire [15:6] multiplexer_4_out_2;

  Decoder #(.enable("false"), .select(2)) decoder_1 (
    .out0(decoder_1_out0), .out1(decoder_1_out1), .sel(in_1));  // open: out2, out3
  // Probe on Mantysa_A
  // Probe on Mantysa_B
  Comparator #(.mode("unsigned"), .width(5)) comparator_1 (
    .a(Wykladnik_A), .b(Wykladnik_B), .lt(comparator_1_lt));  // open: gt, eq
  Comparator #(.mode("unsigned"), .width(10)) comparator_2 (
    .a(Mantysa_B), .b(Mantysa_A), .gt(comparator_2_gt));  // open: eq, lt
  EXPSIGN expsign_1 (
    .add_sub(expsign_1_add_sub), .sign(expsign_1_sign), .signA(Znak_A), .signB(Znak_B),
    .EXP(exponentcalc_1_out_3), .ADDER(and_1_out), .in_1(decoder_1_out1));
  Extend extend_1 (.out_3(ExtA), .in_1(Mantysa_A), .in_2(exponentcalc_1_out_7));
  Extend extend_2 (.out_3(ExtB), .in_1(Mantysa_B), .in_2(exponentcalc_1_out_6));
  ExponentCalc exponentcalc_1 (
    .out_3(exponentcalc_1_out_3), .out_4(exponentcalc_1_out_4), .out_6(exponentcalc_1_out_6),
    .out_7(exponentcalc_1_out_7), .in_1(Wykladnik_A), .in_2(Wykladnik_B));  // open: out_5
  Multiplexer #(.enable("false"), .width(5)) multiplexer_1 (
    .in0(Wykladnik_A), .in1(Wykladnik_B), .out(multiplexer_1_out), .sel(comparator_1_lt));
  or or_1 (or_1_out, decoder_1_out0, decoder_1_out1);
  or or_2 (or_2_out, exponentcalc_1_out_3, and_1_out);
  Shifter shifter_1 (
    .out_6(shifter_1_out_6), .out_5(shifter_1_out_5), .in_3(exponentcalc_1_out_4), .in_4(or_2_out),
    .in_2(ExtB), .in_1(ExtA));
  and and_1 (and_1_out, not_1_out, comparator_2_gt);
  or or_3 (or_3_out, exponentcalc_1_out_4[0], exponentcalc_1_out_4[1], exponentcalc_1_out_4[2], exponentcalc_1_out_4[3]);
  not not_1 (not_1_out, or_3_out);
  not not_2 (not_2_out, or_1_out);
  Op op_1 (
    .carry(op_1_carry), .out_4(op_1_out_4), .A(shifter_1_out_5), .B(shifter_1_out_6),
    .ADD_SUB_7dd12d08(expsign_1_add_sub));  // open: sign
  not not_3 (not_3_out, op_1_carry);
  Adder #(.width(5)) adder_1 (.a({5{1'b0}}), .b(multiplexer_1_out), .out(adder_1_out), .cin(op_1_carry));  // open: cout
  Multiplier multiplier_1 (
    .a(ExtA[15:8]), .b(ExtB[15:8]), .out(multiplier_1_out), .cout(multiplier_1_cout));  // open: cin
  Multiplexer #(.enable("false")) multiplexer_2 (.in0(expsign_1_sign), .in1(xor_1_out), .out(out_8), .sel(not_2_out));
  xor xor_1 (xor_1_out, Znak_A, Znak_B);
  normalizer normalizer_1 (
    .out_3(normalizer_1_out_3), .out_4(normalizer_1_out_4), .out_2(normalizer_1_out_2), .in_1(op_1_out_4));
  and and_2 (and_2_out, normalizer_1_out_4, not_3_out);
  // Probe on {multiplier_1_cout, multiplier_1_out}
  // Probe on multiplexer_4_out
  assign bit_extender_1_out = {{1{1'b0}}, normalizer_1_out_3};  // Bit_Extender bit_extender_1
  Multiplexer #(.enable("false"), .width(5)) multiplexer_3 (
    .in0(bit_extender_1_out), .in1({5{1'b0}}), .out(multiplexer_3_out), .sel(op_1_carry));
  normalizer normalizer_2 (
    .out_3(normalizer_2_out_3), .out_2(normalizer_2_out_2), .in_1({multiplier_1_cout, multiplier_1_out}));  // open: out_4
  Adder #(.width(5)) adder_2 (
    .a(Wykladnik_A), .b(Wykladnik_B), .out(adder_2_out), .cout(adder_2_cout[5]));  // open: cin
  Multiplexer #(.enable("false"), .width(16)) multiplexer_4 (
    .in0(op_1_out_4), .in1(normalizer_1_out_2), .out({multiplexer_4_out_2, multiplexer_4_out}),
    .sel(not_3_out));
  Subtractor #(.width(5)) subtractor_1 (
    .a(adder_1_out), .b(multiplexer_3_out), .out(subtractor_1_out));  // open: bin, bout
  Subtractor #(.width(6)) subtractor_2 (
    .a({adder_2_cout[5], adder_2_out}), .b(6'b001111), .out(subtractor_2_out));  // open: bin, bout
  Multiplexer #(.enable("false"), .width(5)) multiplexer_5 (
    .in0(subtractor_1_out), .in1({5{1'b0}}), .out(multiplexer_5_out), .sel(and_2_out));
  // Probe on normalizer_2_out_2
  // Probe on subtractor_3_out
  // Probe on subtractor_2_out
  Multiplexer #(.enable("false"), .width(10)) multiplexer_6 (
    .in0(multiplexer_4_out_2), .in1(normalizer_2_out_2[15:6]), .out(out_9), .sel(not_2_out));
  Subtractor #(.width(4)) subtractor_3 (
    .a(4'b0001), .b(normalizer_2_out_3), .out(subtractor_3_out));  // open: bin, bout
  Multiplexer #(.enable("false"), .width(5)) multiplexer_7 (
    .in0(multiplexer_5_out), .in1(adder_3_out), .out(out_10), .sel(not_2_out));
  assign bit_extender_2_out = {{1{1'b0}}, subtractor_3_out};  // Bit_Extender bit_extender_2
  Adder #(.width(5)) adder_3 (.a(subtractor_2_out[4:0]), .b(bit_extender_2_out), .out(adder_3_out));  // open: cin, cout
endmodule

module Extend (
  input  [9:0] in_1,
  input  in_2,
  output [15:0] out_3
);

  wire [3:0] multiplexer_2_out;
  wire [10:0] bit_extender_1_out, bit_extender_2_out, multiplexer_1_out;
  wire [15:0] bit_extender_3_out;

  assign bit_extender_1_out = {{1{in_1[9]}}, in_1};  // Bit_Extender bit_extender_1
  Multiplexer #(.enable("false"), .width(11)) multiplexer_1 (
    .in0(bit_extender_1_out), .in1(bit_extender_2_out), .out(multiplexer_1_out), .sel(in_2));
  assign bit_extender_2_out = {{1{1'b1}}, in_1};  // Bit_Extender bit_extender_2
  assign bit_extender_3_out = {{5{multiplexer_1_out[10]}}, multiplexer_1_out};  // Bit_Extender bit_extender_3
  Multiplexer #(.enable("false"), .width(4)) multiplexer_2 (
    .in0(4'b0110), .in1(4'b0101), .out(multiplexer_2_out), .sel(in_2));
  Shifter_part #(.width(16)) shifter_1 (.in(bit_extender_3_out), .\dist (multiplexer_2_out), .out(out_3));
endmodule

module Shifter (
  input  [15:0] in_1,
  input  [15:0] in_2,
  input  [3:0] in_3,
  input  in_4,
  output [15:0] out_5,
  output [15:0] out_6
);

  wire not_1_out;
  wire [15:0] multiplexer_2_out;

  Multiplexer #(.enable("false"), .width(16)) multiplexer_1 (.in0(in_1), .in1(in_2), .out(out_6), .sel(in_4));
  Multiplexer #(.enable("false"), .width(16)) multiplexer_2 (
    .in0(in_1), .in1(in_2), .out(multiplexer_2_out), .sel(not_1_out));
  not not_1 (not_1_out, in_4);
  Shifter_part #(.shift("lr"), .width(16)) shifter_1 (.in(multiplexer_2_out), .\dist (in_3), .out(out_5));
endmodule

module ExponentCalc (
  input  [4:0] in_1,
  input  [4:0] in_2,
  output out_3,
  output [3:0] out_4,
  output [4:0] out_5,
  output out_6,
  output out_7
);

  Subtractor #(.width(5)) subtractor_1 (.a(in_1), .b(in_2), .out({out_3, out_5[3:0]}));  // open: bin, bout
  or or_1 (out_6, in_2[0], in_2[1], in_2[2], in_2[3], in_2[4]);
  or or_2 (out_7, in_1[0], in_1[1], in_1[2], in_1[3], in_1[4]);
  abs abs_1 (.in_1({out_3, out_5[3:0]}), .out_2(out_4));

  assign out_5[4] = out_3;

  // Notes on the sheet:
  //   To są zwykłe addery ustawione na odejmowanie na stałe.
  //   Różnica w U2
  //   To jest bit znaku (czwarty z outputu liczcą od zera)
endmodule

module Op (
  input  ADD_SUB_7dd12d08,
  input  [15:0] A,
  input  [15:0] B,
  output [15:0] out_4,
  output carry,
  output sign
);

  wire adder_1_cout, not_1_out, subtractor_1_bout;
  wire [15:0] adder_1_out, subtractor_1_out;

  Subtractor #(.width(16)) subtractor_1 (.a(B), .b(A), .out(subtractor_1_out), .bout(subtractor_1_bout));  // open: bin
  Adder #(.width(16)) adder_1 (.a(A), .b(B), .out(adder_1_out), .cout(adder_1_cout));  // open: cin
  not not_1 (not_1_out, ADD_SUB_7dd12d08);
  and and_1 (carry, not_1_out, adder_1_cout);
  and and_2 (sign, ADD_SUB_7dd12d08, subtractor_1_bout);
  Multiplexer #(.enable("false"), .width(16)) multiplexer_1 (
    .in0(subtractor_1_out), .in1(adder_1_out), .out(out_4), .sel(not_1_out));
endmodule

module addsub (
  input  in_1,
  input  in_2,
  input  [15:0] a,
  input  [15:0] b,
  output [15:0] out_5,
  output out_6
);

  wire [15:0] adder_1_out, subtractor_1_out, subtractor_2_out;

  Adder #(.width(16)) adder_1 (.a(a), .b(b), .out(adder_1_out), .cout(out_6));  // open: cin
  Subtractor #(.width(16)) subtractor_1 (.a(a), .b(b), .out(subtractor_1_out));  // open: bin, bout
  Subtractor #(.width(16)) subtractor_2 (.a(b), .b(a), .out(subtractor_2_out));  // open: bin, bout
  Multiplexer #(.enable("false"), .select(2), .width(16)) multiplexer_1 (
    .in0(adder_1_out), .in1(subtractor_1_out), .in2(subtractor_2_out), .out(out_5), .sel({in_2, in_1}));  // open: in3
endmodule

module normalizer (
  input  [15:0] in_1,
  output [15:0] out_2,
  output [3:0] out_3,
  output out_4
);

  wire normalizerunit_1_end, normalizerunit_2_end, normalizerunit_3_end, normalizerunit_4_end,
       normalizerunit_5_end, normalizerunit_6_end, normalizerunit_7_end, normalizerunit_8_end,
       normalizerunit_9_end, normalizerunit_10_end, normalizerunit_11_end, normalizerunit_12_end,
       normalizerunit_13_end, normalizerunit_14_end, priority_encoder_1_p17, priority_encoder_1_p18;
  wire [3:0] priority_encoder_1_p10;
  wire [15:0] normalizerunit_1_out, normalizerunit_1_outputbus_2, normalizerunit_2_out,
       normalizerunit_2_outputbus_2, normalizerunit_3_out, normalizerunit_3_outputbus_2,
       normalizerunit_4_out, normalizerunit_4_outputbus_2, normalizerunit_5_out,
       normalizerunit_5_outputbus_2, normalizerunit_6_out, normalizerunit_6_outputbus_2,
       normalizerunit_7_out, normalizerunit_7_outputbus_2, normalizerunit_8_out,
       normalizerunit_8_outputbus_2, normalizerunit_9_out, normalizerunit_9_outputbus_2,
       normalizerunit_10_out, normalizerunit_10_outputbus_2, normalizerunit_11_out,
       normalizerunit_11_outputbus_2, normalizerunit_12_out, normalizerunit_12_outputbus_2,
       normalizerunit_13_out, normalizerunit_13_outputbus_2, normalizerunit_14_out,
       normalizerunit_14_outputbus_2, normalizerunit_15_out, normalizerunit_15_outputbus_2;

  normalizerUnit normalizerunit_1 (
    .In(in_1), .OutputBus({16{1'b0}}), .Out(normalizerunit_1_out), .End(normalizerunit_1_end),
    .OutputBus_2(normalizerunit_1_outputbus_2));
  normalizerUnit normalizerunit_2 (
    .In(normalizerunit_1_out), .OutputBus(normalizerunit_1_outputbus_2), .Out(normalizerunit_2_out),
    .End(normalizerunit_2_end), .OutputBus_2(normalizerunit_2_outputbus_2));
  normalizerUnit normalizerunit_3 (
    .In(normalizerunit_2_out), .OutputBus(normalizerunit_2_outputbus_2), .Out(normalizerunit_3_out),
    .End(normalizerunit_3_end), .OutputBus_2(normalizerunit_3_outputbus_2));
  normalizerUnit normalizerunit_4 (
    .In(normalizerunit_3_out), .OutputBus(normalizerunit_3_outputbus_2), .Out(normalizerunit_4_out),
    .End(normalizerunit_4_end), .OutputBus_2(normalizerunit_4_outputbus_2));
  normalizerUnit normalizerunit_5 (
    .In(normalizerunit_4_out), .OutputBus(normalizerunit_4_outputbus_2), .Out(normalizerunit_5_out),
    .End(normalizerunit_5_end), .OutputBus_2(normalizerunit_5_outputbus_2));
  normalizerUnit normalizerunit_6 (
    .In(normalizerunit_5_out), .OutputBus(normalizerunit_5_outputbus_2), .Out(normalizerunit_6_out),
    .End(normalizerunit_6_end), .OutputBus_2(normalizerunit_6_outputbus_2));
  normalizerUnit normalizerunit_7 (
    .In(normalizerunit_6_out), .OutputBus(normalizerunit_6_outputbus_2), .Out(normalizerunit_7_out),
    .End(normalizerunit_7_end), .OutputBus_2(normalizerunit_7_outputbus_2));
  normalizerUnit normalizerunit_8 (
    .In(normalizerunit_7_out), .OutputBus(normalizerunit_7_outputbus_2), .Out(normalizerunit_8_out),
    .End(normalizerunit_8_end), .OutputBus_2(normalizerunit_8_outputbus_2));
  normalizerUnit normalizerunit_9 (
    .In(normalizerunit_8_out), .OutputBus(normalizerunit_8_outputbus_2), .Out(normalizerunit_9_out),
    .End(normalizerunit_9_end), .OutputBus_2(normalizerunit_9_outputbus_2));
  normalizerUnit normalizerunit_10 (
    .In(normalizerunit_9_out), .OutputBus(normalizerunit_9_outputbus_2), .Out(normalizerunit_10_out),
    .End(normalizerunit_10_end), .OutputBus_2(normalizerunit_10_outputbus_2));
  normalizerUnit normalizerunit_11 (
    .In(normalizerunit_10_out), .OutputBus(normalizerunit_10_outputbus_2), .Out(normalizerunit_11_out),
    .End(normalizerunit_11_end), .OutputBus_2(normalizerunit_11_outputbus_2));
  normalizerUnit normalizerunit_12 (
    .In(normalizerunit_11_out), .OutputBus(normalizerunit_11_outputbus_2), .Out(normalizerunit_12_out),
    .End(normalizerunit_12_end), .OutputBus_2(normalizerunit_12_outputbus_2));
  normalizerUnit normalizerunit_13 (
    .In(normalizerunit_12_out), .OutputBus(normalizerunit_12_outputbus_2), .Out(normalizerunit_13_out),
    .End(normalizerunit_13_end), .OutputBus_2(normalizerunit_13_outputbus_2));
  normalizerUnit normalizerunit_14 (
    .In(normalizerunit_13_out), .OutputBus(normalizerunit_13_outputbus_2), .Out(normalizerunit_14_out),
    .End(normalizerunit_14_end), .OutputBus_2(normalizerunit_14_outputbus_2));
  // Priority_Encoder #(.select(4)) priority_encoder_1: pin names not known; wires that end beside it: out_4, normalizerunit_1_end, normalizerunit_2_end, normalizerunit_3_end, normalizerunit_4_end, normalizerunit_5_end, normalizerunit_6_end, normalizerunit_7_end, normalizerunit_8_end, priority_encoder_1_p10, normalizerunit_9_end, normalizerunit_10_end, normalizerunit_11_end, normalizerunit_12_end, normalizerunit_13_end, normalizerunit_14_end, priority_encoder_1_p17, priority_encoder_1_p18, out_2
  normalizerUnit normalizerunit_15 (
    .In(normalizerunit_14_out), .OutputBus(normalizerunit_14_outputbus_2), .Out(normalizerunit_15_out),
    .End(priority_encoder_1_p17), .OutputBus_2(normalizerunit_15_outputbus_2));
  normalizerUnit normalizerunit_16 (
    .In(normalizerunit_15_out), .OutputBus(normalizerunit_15_outputbus_2), .End(priority_encoder_1_p18),
    .OutputBus_2(out_2));  // open: Out
  Multiplexer #(.enable("false"), .width(4)) multiplexer_1 (
    .in0(priority_encoder_1_p10), .in1(4'b1111), .out(out_3), .sel(out_4));
endmodule

module EXPSIGN (
  input  in_1,
  input  signA,
  input  signB,
  input  EXP,
  input  ADDER,
  output add_sub,
  output sign
);

  wire and_1_out;
  wire [1:1] rom_1_data;

  ROM #(.addrWidth(4), .dataWidth(2), .misaligned("true")) rom_1 (
    .addr({EXP, signB, signA, in_1}), .data({rom_1_data[1], add_sub}));
  and and_1 (and_1_out, in_1, ADDER);
  xor xor_1 (sign, rom_1_data[1], and_1_out);

  // Notes on the sheet:
  //   contents of rom_1 (hex, n*v repeats v):
  //   0 1 3 2 2 0 2 3 0 3
endmodule

module incdec (
  input  in_1,
  input  in_2,
  input  [4:0] in_3,
  output [4:0] out_4
);

  wire and_1_out, not_1_out, not_2_out;
  wire [4:0] adder_1_out, and_2_out, and_3_out, and_4_out, bit_extender_1_out, bit_extender_2_out,
       bit_extender_3_out, subtractor_1_out;

  not not_1 (not_1_out, in_1);
  not not_2 (not_2_out, in_2);
  and and_1 (and_1_out, not_1_out, not_2_out);
  assign bit_extender_1_out = {{4{and_1_out}}, and_1_out};  // Bit_Extender bit_extender_1
  assign bit_extender_2_out = {{4{in_1}}, in_1};  // Bit_Extender bit_extender_2
  assign bit_extender_3_out = {{4{in_2}}, in_2};  // Bit_Extender bit_extender_3
  Adder #(.width(5)) adder_1 (.a(in_3), .b(5'b00001), .out(adder_1_out));  // open: cin, cout
  Subtractor #(.width(5)) subtractor_1 (.a(in_3), .b(5'b00001), .out(subtractor_1_out));  // open: bin, bout
  assign and_2_out = adder_1_out & bit_extender_2_out;  // AND_Gate and_2, 5 bits wide
  assign and_3_out = subtractor_1_out & bit_extender_3_out;  // AND_Gate and_3, 5 bits wide
  assign and_4_out = in_3 & bit_extender_1_out;  // AND_Gate and_4, 5 bits wide
  assign out_4 = and_2_out | and_3_out | and_4_out;  // OR_Gate or_1, 5 bits wide
endmodule
